# Fritzing sketch Ornidia (saved by Fritzing 0.9.3b)
breadboards: 1

parts:
  Adafruit_HUZZAH_ESP8266_Breakout1 = Adafruit HUZZAH ESP8266 Breakout [part_number=2471]
  Componente1 = ACS712 Low Current Sensor Board v12
  Componente2 = ACS712 Low Current Sensor Board v12
  Componente3 = ACS712 Low Current Sensor Board v12
  U1 = 74HC4052 [package=dil16]
  R1 = Rotary Potentiometer (Small) [maximum_resistance=100kΩ package=THT]
  R2 = Resistor [tolerance=±5% resistance=220 package="0805 [SMD]"]  # not connected
  R3 = Resistor [tolerance=±5% resistance=220 package="0805 [SMD]"]  # not connected
  R4 = Resistor [tolerance=±5% resistance=220 package="0805 [SMD]"]  # not connected
  R5 = Resistor [tolerance=±5% resistance=220 package="0805 [SMD]"]  # not connected
  R6 = Resistor [tolerance=±5% resistance=220 package="0805 [SMD]"]  # not connected
  R7 = Resistor [tolerance=±5% resistance=220 package="0805 [SMD]"]  # not connected

nets:
  GND: Adafruit_HUZZAH_ESP8266_Breakout1.GND, Componente1.GND, Componente2.GND, Componente3.GND, U1.INH, U1.GND, R1.leg1
  5V: Adafruit_HUZZAH_ESP8266_Breakout1.V+, Componente1.5V, Componente2.5V, Componente3.5V, U1.VCC, R1.leg2
  N1: Adafruit_HUZZAH_ESP8266_Breakout1.A, U1.X1
  N2: Adafruit_HUZZAH_ESP8266_Breakout1.#5, U1.B
  N3: Componente1.VO, U1.X0
  N4: Componente2.VO, U1.X2
  N5: Componente3.VO, U1.X
  N6: U1.X3, R1.wiper
